// Logisim project SOMADOR.circ as structural Verilog: 3 circuits, main circuit main
module main (
  input  [2:0] A,
  input  [2:0] B,
  output S3,
  output S2,
  output S1,
  output S0
);

  wire som_comp_1_ts, som_comp_3_ts;

  som_comp som_comp_1 (.Te(som_comp_3_ts), .A(A[1]), .B(B[1]), .S(S1), .Ts(som_comp_1_ts));
  som_comp som_comp_2 (.Te(som_comp_1_ts), .A(A[2]), .B(B[2]), .S(S2), .Ts(S3));
  som_comp som_comp_3 (.Te(1'b0), .A(A[0]), .B(B[0]), .S(S0), .Ts(som_comp_3_ts));
endmodule

module som_comp (
  input  Te,
  input  A,
  input  B,
  output S,
  output Ts
);

  wire and_1_out, and_2_out, and_3_out, and_4_out, and_5_out, and_6_out, and_7_out, not_1_out, not_2_out,
       not_3_out, not_4_out, not_5_out, not_6_out;

  not not_1 (not_1_out, Te);
  not not_2 (not_2_out, A);
  not not_3 (not_3_out, Te);
  not not_4 (not_4_out, B);
  not not_5 (not_5_out, A);
  not not_6 (not_6_out, B);
  and and_1 (and_1_out, A, B);
  and and_2 (and_2_out, Te, B);
  and and_3 (and_3_out, Te, A);
  and and_4 (and_4_out, not_1_out, not_2_out, B);
  and and_5 (and_5_out, not_3_out, A, not_4_out);
  and and_6 (and_6_out, Te, not_5_out, not_6_out);
  and and_7 (and_7_out, Te, A, B);
  or or_1 (Ts, and_1_out, and_2_out, and_3_out);
  or or_2 (S, and_4_out, and_5_out, and_6_out, and_7_out);
endmodule

module meio_som (
  input  A,
  input  B,
  output S,
  output Ts
);

  xor xor_1 (S, A, B);
  and and_1 (Ts, A, B);
endmodule
