// Logisim project circuitos_básicos.circ as structural Verilog: 9 circuits, main circuit main
module main (
  input  I0,
  input  I1,
  input  I2,
  input  I3,
  input  S3,
  input  S2,
  input  S1,
  input  S0,
  input  A,
  input  B,
  input  C,
  input  IN,
  input  S2_2,
  input  S1_2,
  input  S0_2,
  output D0,
  output D1,
  output D2,
  output D3,
  output OUT_0,
  output OUT_1,
  output OUT_2,
  output out_23,
  output OUT_3,
  output OUT_4,
  output OUT_5,
  output OUT_6,
  output OUT_7
);

  wire and_1_out, and_2_out, demux2_1_out_3, demux2_1_out_4, mux_4_1_out_7, nor_1_out, not_1_out, not_2_out;

  not not_1 (not_1_out, B);
  MUX_4 mux_4_1 (.in_1(I0), .in_2(I1), .in_3(I2), .in_4(I3), .in_5(S3), .in_6(S2), .out_7(mux_4_1_out_7));
  and and_1 (and_1_out, not_1_out, C);
  not not_2 (not_2_out, A);
  and and_2 (and_2_out, A, B);
  nor nor_1 (nor_1_out, B, C);
  demux_4 demux_4_1 (.in_1(mux_4_1_out_7), .D0(D0), .D1(D1), .D2(D2), .D3(D3), .S1(S1), .S0(S0));
  MUX_4 mux_4_2 (
    .in_1(C), .in_2(and_1_out), .in_3(and_2_out), .in_4(not_2_out), .in_5(nor_1_out), .in_6(A), .out_7(out_23));
  DEMUX2 demux2_1 (.in_1(IN), .in_2(S2_2), .out_3(demux2_1_out_3), .out_4(demux2_1_out_4));
  demux_4 demux_4_2 (.in_1(demux2_1_out_3), .D0(OUT_0), .D1(OUT_1), .D2(OUT_2), .D3(OUT_3), .S1(S1_2), .S0(S0_2));
  demux_4 demux_4_3 (.in_1(demux2_1_out_4), .D0(OUT_4), .D1(OUT_5), .D2(OUT_6), .D3(OUT_7), .S1(S1_2), .S0(S0_2));

  // Notes on the sheet:
  //   MUX_4
  //   DEMUX_4
  //   DEMUX_2
  //   DEMUX_4
  //   DEMUX_4
endmodule

module demux_4 (
  input  in_1,
  input  S1,
  input  S0,
  output D0,
  output D1,
  output D2,
  output D3
);

  wire not_1_out, not_2_out, not_3_out;

  not not_1 (not_1_out, S1);
  not not_2 (not_2_out, S0);
  not not_3 (not_3_out, S0);
  and and_1 (D0, not_1_out, not_2_out, in_1);
  and and_2 (D1, not_1_out, S0, in_1);
  and and_3 (D2, S1, not_3_out, in_1);
  and and_4 (D3, S1, S0, in_1);
endmodule

module DEMUX2 (
  input  in_1,
  input  in_2,
  output out_3,
  output out_4
);

  wire not_1_out;

  not not_1 (not_1_out, in_2);
  and and_1 (out_3, not_1_out, in_1);
  and and_2 (out_4, in_2, in_1);
endmodule

module MUX_4 (
  input  in_1,
  input  in_2,
  input  in_3,
  input  in_4,
  input  in_5,
  input  in_6,
  output out_7
);

  wire and_1_out, and_2_out, and_3_out, and_4_out, not_1_out, not_2_out, not_3_out;

  not not_1 (not_1_out, in_5);
  not not_2 (not_2_out, in_6);
  not not_3 (not_3_out, in_6);
  and and_1 (and_1_out, not_1_out, not_2_out, in_1);
  and and_2 (and_2_out, not_1_out, in_6, in_2);
  and and_3 (and_3_out, in_5, not_3_out, in_3);
  and and_4 (and_4_out, in_5, in_6, in_4);
  or or_1 (out_7, and_1_out, and_2_out, and_3_out, and_4_out);
endmodule

module memoria (
  input  [4:0] \Endereço ,
  input  Sel,
  output [15:0] out_3
);

  wire not_1_out;

  not not_1 (not_1_out, Sel);
  ROM #(.addrWidth(5), .dataWidth(16)) rom_1 (.addr(\Endereço ), .data(out_3), .sel(not_1_out));
  ROM #(.addrWidth(5), .dataWidth(16)) rom_2 (.addr(\Endereço ), .data(out_3), .sel(Sel));

  // Notes on the sheet:
  //   contents of rom_2 (hex, n*v repeats v):
  //   30*0 8
endmodule

module CONTADOR_ASSINCRONO (
  input  in_1,
  input  in_2,
  input  in_3,
  input  in_4,
  input  in_5,
  output out_6,
  output out_7
);

  wire and_1_out, j_k_ff_1_q, j_k_ff_2_q, j_k_ff_3_q, j_k_ff_4_q, not_1_out, xor_1_out;

  and and_1 (and_1_out, j_k_ff_2_q, j_k_ff_4_q);
  not not_1 (not_1_out, out_6);
  J_K_Flip_Flop #(.trigger("falling")) j_k_ff_1 (
    .J(in_1), .clk(in_2), .K(in_1), .Q(j_k_ff_1_q), .en(in_3), .reset(and_1_out));  // open: Qn, preset
  D_Flip_Flop d_ff_1 (.clk(in_4), .D(not_1_out), .Q(out_6), .en(in_5));  // open: Qn, preset, reset
  D_Flip_Flop d_ff_2 (.clk(in_4), .D(xor_1_out), .Q(out_7), .en(in_5));  // open: Qn, preset, reset
  J_K_Flip_Flop #(.trigger("falling")) j_k_ff_2 (
    .J(in_1), .clk(j_k_ff_1_q), .K(in_1), .Q(j_k_ff_2_q), .en(in_3), .reset(and_1_out));  // open: Qn, preset
  J_K_Flip_Flop #(.trigger("falling")) j_k_ff_3 (
    .J(in_1), .clk(j_k_ff_2_q), .K(in_1), .Q(j_k_ff_3_q), .en(in_3), .reset(and_1_out));  // open: Qn, preset
  xor xor_1 (xor_1_out, out_6, out_7);
  J_K_Flip_Flop #(.trigger("falling")) j_k_ff_4 (
    .J(in_1), .clk(j_k_ff_3_q), .K(in_1), .Q(j_k_ff_4_q), .en(in_3), .reset(and_1_out));  // open: Qn, preset
endmodule

module registrador (
  input  CLK,
  input  CLR,
  input  PRST,
  input  IN_3,
  input  IN_2,
  input  IN_1,
  input  IN_0,
  output OUT
);

  wire and_1_out, and_2_out, and_3_out, and_4_out, d_ff_1_q, d_ff_2_q, d_ff_3_q;

  and and_1 (and_1_out, PRST, IN_3);
  D_Flip_Flop d_ff_1 (.clk(CLK), .D(1'b0), .Q(d_ff_1_q), .preset(and_1_out), .reset(CLR));  // open: Qn, en
  and and_2 (and_2_out, PRST, IN_2);
  D_Flip_Flop d_ff_2 (.clk(CLK), .D(d_ff_1_q), .Q(d_ff_2_q), .preset(and_2_out), .reset(CLR));  // open: Qn, en
  and and_3 (and_3_out, PRST, IN_1);
  D_Flip_Flop d_ff_3 (.clk(CLK), .D(d_ff_2_q), .Q(d_ff_3_q), .preset(and_3_out), .reset(CLR));  // open: Qn, en
  and and_4 (and_4_out, PRST, IN_0);
  D_Flip_Flop d_ff_4 (.clk(CLK), .D(d_ff_3_q), .Q(OUT), .preset(and_4_out), .reset(CLR));  // open: Qn, en
endmodule

module ASSINCRONO_REVERSIVEL (
  input  H,
  input  CLK,
  input  IN,
  output Q2,
  output Q1,
  output Q0
);

  wire and_1_out, and_2_out, and_3_out, and_4_out, and_5_out, t_ff_1_qn, t_ff_2_qn, xor_1_out, xor_2_out;

  T_Flip_Flop #(.trigger("falling")) t_ff_1 (
    .clk(CLK), .T(IN), .Q(Q0), .Qn(t_ff_1_qn), .reset(and_1_out));  // open: preset, en
  and and_1 (and_1_out, Q2, ~Q1, Q0);  // AND_Gate
  and and_2 (and_2_out, ~H, Q0);  // AND_Gate
  xor xor_1 (xor_1_out, and_2_out, and_3_out);
  and and_3 (and_3_out, t_ff_1_qn, H);
  T_Flip_Flop #(.trigger("falling")) t_ff_2 (
    .clk(xor_1_out), .T(IN), .Q(Q1), .Qn(t_ff_2_qn), .reset(and_1_out));  // open: preset, en
  and and_4 (and_4_out, ~H, Q1);  // AND_Gate
  and and_5 (and_5_out, t_ff_2_qn, H);
  T_Flip_Flop #(.trigger("falling")) t_ff_3 (
    .clk(xor_2_out), .T(IN), .Q(Q2), .reset(and_1_out));  // open: Qn, preset, en
  xor xor_2 (xor_2_out, and_4_out, and_5_out);
endmodule

module DEMUX_16 (
  input  IN,
  input  SEL_3,
  input  SEL_2,
  input  SEL_1,
  input  SEL_0,
  output OUT_0,
  output OUT_1,
  output OUT_2,
  output OUT_3,
  output OUT_4,
  output OUT_5,
  output OUT_6,
  output OUT_7,
  output OUT_8,
  output OUT_9,
  output OUT_10,
  output OUT_11,
  output OUT_12,
  output OUT_13,
  output OUT_14,
  output OUT_15
);

  wire demux_4_1_d0, demux_4_1_d1, demux_4_1_d2, demux_4_1_d3;

  demux_4 demux_4_1 (
    .in_1(IN), .D0(demux_4_1_d0), .D1(demux_4_1_d1), .D2(demux_4_1_d2), .D3(demux_4_1_d3), .S1(SEL_3),
    .S0(SEL_2));
  demux_4 demux_4_2 (.in_1(demux_4_1_d0), .D0(OUT_0), .D1(OUT_1), .D2(OUT_2), .D3(OUT_3), .S1(SEL_1), .S0(SEL_0));
  demux_4 demux_4_3 (.in_1(demux_4_1_d1), .D0(OUT_4), .D1(OUT_5), .D2(OUT_6), .D3(OUT_7), .S1(SEL_1), .S0(SEL_0));
  demux_4 demux_4_4 (.in_1(demux_4_1_d2), .D0(OUT_8), .D1(OUT_9), .D2(OUT_10), .D3(OUT_11), .S1(SEL_1), .S0(SEL_0));
  demux_4 demux_4_5 (.in_1(demux_4_1_d3), .D0(OUT_12), .D1(OUT_13), .D2(OUT_14), .D3(OUT_15), .S1(SEL_1), .S0(SEL_0));
endmodule
